// Logisim project brainfuck_machine.circ as structural Verilog: 1 circuit, main circuit main
module main (
  input  [7:0] EXT_INPUT,
  input  OUTPUT_READY,
  output [7:0] EXT_OUTPUT,
  output CLK
);

  wire and_1_out, and_2_out, and_3_out, and_4_out, and_5_out, and_6_out, and_7_out, and_8_out, and_9_out,
       and_10_out, clock_1_out, clock_2_out, clock_3_out, clock_4_out, clock_5_out, clock_6_out, clock_7_out,
       clock_8_out, clock_9_out, clock_10_out, clock_11_out, clock_12_out, comparator_1_eq, comparator_2_eq,
       comparator_3_eq, comparator_4_eq, comparator_5_eq, comparator_6_eq, d_ff_1_q, d_ff_2_q, d_ff_3_q,
       d_ff_4_q, nor_1_out, nor_2_out, nor_3_out, nor_4_out, not_1_out, not_2_out, not_3_out, not_4_out,
       not_5_out, not_6_out, not_7_out, or_1_out, or_2_out, RESET_out, STARTUP_qn;
  wire [0:0] comparator_7_eq, EXT_CLK_out;
  wire [7:0] adder_1_out, R_IN_q, R_OUT_q, ram_1_data, register_1_q, register_2_q, rom_1_data,
       subtractor_1_out;
  wire [14:0] counter_1_q, counter_2_q;

  Button RESET (.out(RESET_out));
  D_Flip_Flop STARTUP (.D(1'b1), .clk(clock_1_out), .Qn(STARTUP_qn), .reset(RESET_out));  // open: Q, preset
  Clock clock_1 (.out(clock_1_out));
  nor nor_1 (nor_1_out, comparator_1_eq, STARTUP_qn, d_ff_2_q, d_ff_4_q);
  nor nor_2 (nor_2_out, STARTUP_qn, d_ff_2_q, d_ff_4_q);
  and and_1 (and_1_out, or_2_out, nor_2_out);
  Counter #(.max('h7fff), .width(15)) counter_1 (
    .clr(RESET_out), .count(nor_1_out), .clk(clock_2_out), .Q(counter_1_q));  // open: load, up, D, carry
  Clock clock_2 (.out(clock_2_out));
  Counter #(.max('h7fff), .trigger("falling"), .width(15)) counter_2 (
    .clr(RESET_out), .up(comparator_2_eq), .count(and_1_out), .clk(clock_3_out), .Q(counter_2_q));  // open: load, D, carry
  Clock clock_3 (.out(clock_3_out));
  not not_1 (not_1_out, and_2_out);
  Clock clock_4 (.out(clock_4_out));
  ROM #(.addrWidth(15)) rom_1 (.addr(counter_1_q), .data(rom_1_data));
  RAM #(.addrWidth(15), .asyncread("true"), .clearpin("true"), .databus("bidir"), .trigger("falling")) ram_1 (
    .addr(counter_2_q), .we(and_2_out), .oe(not_1_out), .clk(clock_4_out), .data(ram_1_data), .clr(RESET_out));
  Adder adder_1 (.a(ram_1_data), .b(8'h1), .out(adder_1_out));  // open: cin, cout
  Subtractor subtractor_1 (.a(ram_1_data), .b(8'h1), .out(subtractor_1_out));  // open: bin, bout
  Comparator comparator_1 (.a(rom_1_data), .b({8{1'b0}}), .eq(comparator_1_eq));  // open: gt, lt
  Comparator comparator_2 (.a(rom_1_data), .b(8'h3e), .eq(comparator_2_eq));  // open: gt, lt
  Comparator comparator_3 (.a(rom_1_data), .b(8'h3c), .eq(comparator_3_eq));  // open: gt, lt
  Comparator comparator_4 (.a(rom_1_data), .b(8'h2b), .eq(comparator_4_eq));  // open: gt, lt
  Comparator comparator_5 (.a(rom_1_data), .b(8'h2d), .eq(comparator_5_eq));  // open: gt, lt
  Comparator comparator_6 (.a(rom_1_data), .b(8'h2e), .eq(comparator_6_eq));  // open: gt, lt
  Comparator comparator_7 (.a(rom_1_data), .b(8'h2c), .eq(comparator_7_eq[0]));  // open: gt, lt
  Comparator comparator_8 (.a(rom_1_data), .b(8'h5b));  // open: gt, eq, lt
  Comparator comparator_9 (.a(rom_1_data), .b(8'h5d));  // open: gt, eq, lt
  Register register_1 (.D(adder_1_out), .clk(clock_5_out), .Q(register_1_q));  // open: en, clr
  Clock clock_5 (.out(clock_5_out));
  Register register_2 (.D(subtractor_1_out), .clk(clock_6_out), .Q(register_2_q));  // open: en, clr
  Clock clock_6 (.out(clock_6_out));
  Clock clock_7 (.out(clock_7_out));
  Clock clock_8 (.out(clock_8_out));
  assign ram_1_data = comparator_4_eq ? register_1_q : 8'bz;  // Controlled_Buffer controlled_buffer_1
  assign ram_1_data = comparator_5_eq ? register_2_q : 8'bz;  // Controlled_Buffer controlled_buffer_2
  not not_2 (not_2_out, clock_7_out);
  not not_3 (not_3_out, clock_8_out);
  or or_1 (or_1_out, comparator_4_eq, comparator_5_eq, comparator_7_eq[0]);
  and and_2 (and_2_out, or_1_out, nor_2_out);
  and and_3 (and_3_out, nor_2_out, comparator_7_eq[0]);
  assign ram_1_data = and_3_out ? R_IN_q : 8'bz;  // Controlled_Buffer controlled_buffer_3
  nor nor_3 (nor_3_out, not_2_out, clock_7_out);
  and and_4 (and_4_out, not_3_out, clock_8_out);
  Clock clock_9 (.out(clock_9_out));
  or or_2 (or_2_out, comparator_2_eq, comparator_3_eq);
  not not_4 (not_4_out, clock_9_out);
  not not_5 (not_5_out, clock_10_out);
  Clock clock_10 (.out(clock_10_out));
  not not_6 (not_6_out, OUTPUT_READY);
  nor nor_4 (nor_4_out, not_4_out, clock_9_out);
  and and_5 (and_5_out, not_5_out, clock_10_out);
  D_Flip_Flop #(.trigger("falling")) d_ff_1 (
    .D(1'b0), .clk(clock_11_out), .Q(d_ff_1_q), .preset(and_6_out));  // open: Qn, reset
  Clock clock_11 (.out(clock_11_out));
  and and_6 (and_6_out, OUTPUT_READY, nor_3_out, comparator_6_eq);
  and and_7 (and_7_out, not_6_out, nor_3_out, comparator_6_eq);
  D_Flip_Flop d_ff_2 (.Q(d_ff_2_q), .preset(and_7_out), .reset(and_8_out));  // open: D, clk, Qn
  and and_8 (and_8_out, OUTPUT_READY, and_4_out);
  Register #(.trigger("falling")) R_OUT (
    .D(ram_1_data), .en(comparator_6_eq), .clk(clock_12_out), .Q(R_OUT_q));  // open: clr
  Clock clock_12 (.out(clock_12_out));
  Register R_IN (.D(EXT_OUTPUT), .en(comparator_7_eq[0]), .clk(CLK), .Q(R_IN_q));  // open: clr
  D_Flip_Flop #(.trigger("falling")) d_ff_3 (.Q(d_ff_3_q), .preset(CLK), .reset(and_10_out));  // open: D, clk, Qn
  not not_7 (not_7_out, d_ff_3_q);
  and and_9 (and_9_out, comparator_7_eq[0], not_7_out, nor_4_out);
  and and_10 (and_10_out, d_ff_3_q, and_5_out);
  D_Flip_Flop d_ff_4 (.Q(d_ff_4_q), .preset(and_9_out), .reset(and_10_out));  // open: D, clk, Qn
  assign EXT_OUTPUT = comparator_6_eq ? R_OUT_q : 8'bz;  // Controlled_Buffer controlled_buffer_4
  assign CLK = comparator_6_eq ? d_ff_1_q : 1'bz;  // Controlled_Buffer controlled_buffer_5
  assign {EXT_OUTPUT, CLK} = comparator_7_eq[0] ? {EXT_INPUT, EXT_CLK_out[0]} : 9'bz;  // Controlled_Buffer controlled_buffer_6
  Button EXT_CLK (.out(EXT_CLK_out[0]));

  // Notes on the sheet:
  //   contents of rom_1 (hex, n*v repeats v):
  //   2b 2b 3e 2c 2e 3c 2d 2d
  //   \0
  //   >
  //   <
  //   +
  //   -
  //   .
  //   ,
  //   [
  //   ]
  //   OE
  //   IE
  //   State OUTPUT
  //   State INPUT
endmodule
